// Logisim project 01.circ as structural Verilog: 7 circuits, main circuit AND
module AND (
  input  a,
  input  b,
  output out
);

  wire nand_1_out;

  nand nand_1 (nand_1_out, a, b);
  not nand_2 (out, nand_1_out);  // NAND_Gate
endmodule

module NOT (
  input  in,
  output out
);

  not nand_1 (out, in);  // NAND_Gate
endmodule

module OR (
  input  a,
  input  b,
  output out
);

  wire not_1_out, not_2_out;

  not not_1 (not_1_out, a);
  not not_2 (not_2_out, b);
  nand nand_1 (out, not_1_out, not_2_out);
endmodule

module Mux (
  input  Sel,
  input  a,
  input  b,
  output o
);

  wire nand_1_out, nand_2_out, nand_3_out;

  nand nand_1 (nand_1_out, a, nand_2_out);
  not nand_2 (nand_2_out, Sel);  // NAND_Gate
  nand nand_3 (nand_3_out, Sel, b);
  nand nand_4 (o, nand_1_out, nand_3_out);
endmodule

module DMux (
  input  sel,
  input  in,
  output a,
  output b
);

  wire nand_1_out, nand_2_out, nand_4_out;

  not nand_1 (nand_1_out, sel);  // NAND_Gate
  nand nand_2 (nand_2_out, nand_1_out, in);
  not nand_3 (a, nand_2_out);  // NAND_Gate
  nand nand_4 (nand_4_out, sel, in);
  not nand_5 (b, nand_4_out);  // NAND_Gate
endmodule

module OR16way (
  input  [15:0] in,
  output out
);

  or or_1 (out, in[0], in[1], in[2], in[3], in[4], in[5], in[6], in[7], in[8], in[9], in[10], in[11], in[12], in[13], in[14], in[15]);
endmodule

module DMux16way (
  input  [15:0] in,
  output out_2
);
endmodule
