// Logisim project 02.circ as structural Verilog: 5 circuits, main circuit HalfAdder
module HalfAdder (
  input  a,
  input  b,
  output sum,
  output carry
);

  xor xor_1 (sum, a, b);
  and and_1 (carry, a, b);
endmodule

module FullAdder (
  input  carryIn,
  input  a,
  input  b,
  output sum,
  output carryOut
);

  wire halfadder_1_carry, halfadder_1_sum, halfadder_2_carry;

  Pull_Resistor pull_resistor_1 (.node(carryIn));
  HalfAdder halfadder_1 (.a(a), .b(b), .sum(halfadder_1_sum), .carry(halfadder_1_carry));
  HalfAdder halfadder_2 (.a(carryIn), .b(halfadder_1_sum), .sum(sum), .carry(halfadder_2_carry));
  or or_1 (carryOut, halfadder_2_carry, halfadder_1_carry);
endmodule

module Add16 (
  input  carryIn,
  input  [15:0] in_2,
  input  [15:0] in_3,
  output [15:0] out_4,
  output carryOut
);

  wire fulladder_1_carryout, fulladder_2_carryout, fulladder_3_carryout, fulladder_4_carryout,
       fulladder_5_carryout, fulladder_6_carryout, fulladder_7_carryout, fulladder_8_carryout,
       fulladder_9_carryout, fulladder_10_carryout, fulladder_11_carryout, fulladder_12_carryout,
       fulladder_13_carryout, fulladder_14_carryout, fulladder_15_carryout;

  FullAdder fulladder_1 (.a(in_2[0]), .b(in_3[0]), .sum(out_4[0]), .carryIn(carryIn), .carryOut(fulladder_1_carryout));
  FullAdder fulladder_2 (
    .a(in_2[1]), .b(in_3[1]), .sum(out_4[1]), .carryIn(fulladder_1_carryout), .carryOut(fulladder_2_carryout));
  FullAdder fulladder_3 (
    .a(in_2[2]), .b(in_3[2]), .sum(out_4[2]), .carryIn(fulladder_2_carryout), .carryOut(fulladder_3_carryout));
  FullAdder fulladder_4 (
    .a(in_2[3]), .b(in_3[3]), .sum(out_4[3]), .carryIn(fulladder_3_carryout), .carryOut(fulladder_4_carryout));
  FullAdder fulladder_5 (
    .a(in_2[4]), .b(in_3[4]), .sum(out_4[4]), .carryIn(fulladder_4_carryout), .carryOut(fulladder_5_carryout));
  FullAdder fulladder_6 (
    .a(in_2[5]), .b(in_3[5]), .sum(out_4[5]), .carryIn(fulladder_5_carryout), .carryOut(fulladder_6_carryout));
  FullAdder fulladder_7 (
    .a(in_2[6]), .b(in_3[6]), .sum(out_4[6]), .carryIn(fulladder_6_carryout), .carryOut(fulladder_7_carryout));
  FullAdder fulladder_8 (
    .a(in_2[7]), .b(in_3[7]), .sum(out_4[7]), .carryIn(fulladder_7_carryout), .carryOut(fulladder_8_carryout));
  FullAdder fulladder_9 (
    .a(in_2[8]), .b(in_3[8]), .sum(out_4[8]), .carryIn(fulladder_8_carryout), .carryOut(fulladder_9_carryout));
  FullAdder fulladder_10 (
    .a(in_2[9]), .b(in_3[9]), .sum(out_4[9]), .carryIn(fulladder_9_carryout), .carryOut(fulladder_10_carryout));
  FullAdder fulladder_11 (
    .a(in_2[10]), .b(in_3[10]), .sum(out_4[10]), .carryIn(fulladder_10_carryout),
    .carryOut(fulladder_11_carryout));
  FullAdder fulladder_12 (
    .a(in_2[11]), .b(in_3[11]), .sum(out_4[11]), .carryIn(fulladder_11_carryout),
    .carryOut(fulladder_12_carryout));
  FullAdder fulladder_13 (
    .a(in_2[12]), .b(in_3[12]), .sum(out_4[12]), .carryIn(fulladder_12_carryout),
    .carryOut(fulladder_13_carryout));
  FullAdder fulladder_14 (
    .a(in_2[13]), .b(in_3[13]), .sum(out_4[13]), .carryIn(fulladder_13_carryout),
    .carryOut(fulladder_14_carryout));
  FullAdder fulladder_15 (
    .a(in_2[14]), .b(in_3[14]), .sum(out_4[14]), .carryIn(fulladder_14_carryout),
    .carryOut(fulladder_15_carryout));
  FullAdder fulladder_16 (
    .a(in_2[15]), .b(in_3[15]), .sum(out_4[15]), .carryIn(fulladder_15_carryout), .carryOut(carryOut));
endmodule

module Inc16 (
  input  [15:0] in,
  output [15:0] out,
  output carryOut
);

  Add16 add16_1 (.in_2(in), .in_3(16'h1), .out_4(out), .carryOut(carryOut));  // open: carryIn
endmodule

module ALU (
  input  zx,
  input  zy,
  input  nx,
  input  ny,
  input  f,
  input  no,
  input  [15:0] x,
  input  [15:0] y,
  output [15:0] out,
  output zr,
  output ng
);

  wire or16way_1_out;
  wire [15:0] add16_1_out_4, and_1_out, multiplexer_1_out, multiplexer_2_out, multiplexer_3_out,
       multiplexer_4_out, multiplexer_5_out, not_1_out, not_2_out, not_3_out;

  Multiplexer #(.width(16), .enable("false")) multiplexer_1 (
    .in0(x), .in1({16{1'b0}}), .out(multiplexer_1_out), .sel(zx));
  assign not_1_out = ~multiplexer_1_out;  // NOT_Gate not_1, 16 bits wide
  Multiplexer #(.width(16), .enable("false")) multiplexer_2 (
    .in0(y), .in1({16{1'b0}}), .out(multiplexer_2_out), .sel(zy));
  assign not_2_out = ~multiplexer_2_out;  // NOT_Gate not_2, 16 bits wide
  Multiplexer #(.width(16), .enable("false")) multiplexer_3 (
    .in0(multiplexer_1_out), .in1(not_1_out), .out(multiplexer_3_out), .sel(nx));
  Multiplexer #(.width(16), .enable("false")) multiplexer_4 (
    .in0(multiplexer_2_out), .in1(not_2_out), .out(multiplexer_4_out), .sel(ny));
  assign and_1_out = multiplexer_3_out & multiplexer_4_out;  // AND_Gate and_1, 16 bits wide
  Add16 add16_1 (.in_2(multiplexer_3_out), .in_3(multiplexer_4_out), .out_4(add16_1_out_4));  // open: carryIn, carryOut
  Multiplexer #(.width(16), .enable("false")) multiplexer_5 (
    .in0(and_1_out), .in1(add16_1_out_4), .out(multiplexer_5_out), .sel(f));
  assign not_3_out = ~multiplexer_5_out;  // NOT_Gate not_3, 16 bits wide
  OR16way or16way_1 (.in({ng, out[14:0]}), .out(or16way_1_out));
  not not_4 (zr, or16way_1_out);
  Multiplexer #(.width(16), .enable("false")) multiplexer_6 (
    .in0(multiplexer_5_out), .in1(not_3_out), .out({ng, out[14:0]}), .sel(no));

  assign out[15] = ng;
endmodule
