// Logisim project 05.circ as structural Verilog: 4 circuits, main circuit CPU
module CPU (
  input  [15:0] inM,
  input  [15:0] instruction,
  input  reset,
  output [15:0] outM,
  output [14:0] addressM,
  output writeM,
  output [14:0] pc
);

  wire alu_1_ng, alu_1_zr, ck, control_1_abit, control_1_ainst, jmpctrl_1_jump, or_1_out;
  wire [2:0] control_1_jump;
  wire [2:1] control_1_dest;
  wire [5:0] control_1_cbits;
  wire [14:0] control_1_value;
  wire [15:0] D_q, multiplexer_1_out, multiplexer_2_out;
  wire [15:15] A_q, pc_1_out;

  // Probe on inM
  // Probe on instruction
  Clock clock_1 (.out(ck));
  Control control_1 (
    .instruction(instruction), .AInst(control_1_ainst), .value(control_1_value), .abit(control_1_abit),
    .cbits(control_1_cbits), .dest({control_1_dest, writeM}), .jump(control_1_jump));
  Multiplexer #(.width(16), .enable("false")) multiplexer_1 (
    .in0(outM), .in1({1'b0, control_1_value}), .out(multiplexer_1_out), .sel(control_1_ainst));
  or or_1 (or_1_out, control_1_ainst, control_1_dest[2]);
  Register #(.width(16)) A (.D(multiplexer_1_out), .en(or_1_out), .Q({A_q[15], addressM}), .clk(ck));  // open: clr
  Multiplexer #(.width(16), .enable("false")) multiplexer_2 (
    .in0({A_q[15], addressM}), .in1(inM), .out(multiplexer_2_out), .sel(control_1_abit));
  Register #(.width(16)) D (.D(outM), .en(control_1_dest[1]), .Q(D_q), .clk(ck));  // open: clr
  ALU alu_1 (
    .x(D_q), .y(multiplexer_2_out), .out(outM), .zx(control_1_cbits[5]), .zy(control_1_cbits[3]),
    .nx(control_1_cbits[4]), .ny(control_1_cbits[2]), .f(control_1_cbits[1]), .no(control_1_cbits[0]),
    .zr(alu_1_zr), .ng(alu_1_ng));
  JmpCtrl jmpctrl_1 (
    .lt(control_1_jump[0]), .eq(control_1_jump[1]), .gt(control_1_jump[2]), .jump(jmpctrl_1_jump),
    .zr(alu_1_zr), .ng(alu_1_ng));
  // Probe on outM
  PC pc_1 (
    .in({A_q[15], addressM}), .out({pc_1_out[15], pc}), .inc(1'b1), .load(jmpctrl_1_jump), .reset(reset),
    .clock(ck));
  // Probe on outM
  // Probe on addressM
  // Probe on pc
endmodule

module Control (
  input  [15:0] instruction,
  output AInst,
  output [14:0] value,
  output abit,
  output [5:0] cbits,
  output [2:0] dest,
  output [2:0] jump
);

  wire [15:13] demultiplexer_1_out1;
  wire [15:15] demultiplexer_1_out0;

  Demultiplexer #(.width(16), .enable("false")) demultiplexer_1 (
    .out0({demultiplexer_1_out0[15], value}), .out1({demultiplexer_1_out1, abit, cbits, dest, jump}),
    .in(instruction), .sel(instruction[15]));
  not not_1 (AInst, instruction[15]);
endmodule

module PC (
  input  inc,
  input  load,
  input  reset,
  input  [15:0] in,
  input  clock,
  output [15:0] out
);

  wire [15:0] inc16_1_out, multiplexer_1_out, multiplexer_2_out, multiplexer_3_out;

  Multiplexer #(.width(16), .enable("false")) multiplexer_1 (
    .in0(out), .in1(inc16_1_out), .out(multiplexer_1_out), .sel(inc));
  Inc16 inc16_1 (.in(out), .out(inc16_1_out));  // open: carryOut
  Multiplexer #(.width(16), .enable("false")) multiplexer_2 (
    .in0(multiplexer_1_out), .in1(in), .out(multiplexer_2_out), .sel(load));
  Multiplexer #(.width(16), .enable("false")) multiplexer_3 (
    .in0(multiplexer_2_out), .in1({16{1'b0}}), .out(multiplexer_3_out), .sel(reset));
  Register #(.width(16)) register_1 (.D(multiplexer_3_out), .en(1'b1), .Q(out), .clk(clock));  // open: clr
endmodule

module JmpCtrl (
  input  zr,
  input  ng,
  input  lt,
  input  eq,
  input  gt,
  output jump
);

  wire and_1_out, and_2_out, and_3_out, and_4_out, not_1_out, not_2_out;

  not not_1 (not_1_out, ng);
  and and_1 (and_1_out, not_1_out, not_2_out);
  not not_2 (not_2_out, zr);
  and and_2 (and_2_out, lt, ng);
  or or_1 (jump, and_2_out, and_3_out, and_4_out);
  and and_3 (and_3_out, zr, eq);
  and and_4 (and_4_out, and_1_out, gt);
endmodule
